# Fritzing sketch Jarolator (saved by Fritzing 0.9.5d)
circuit board: 8.46667cm x 5.79277cm
breadboards: 2

parts:
  R2 = Resistor [tolerance=±5% resistance=10k package=THT]
  R3 = Resistor [tolerance=±5% resistance=10k package=THT]
  R4 = Resistor [tolerance=±5% resistance=10k package=THT]
  R5 = Resistor [tolerance=±5% resistance=10k package=THT]
  R6 = Resistor [tolerance=±5% resistance=12k package=THT]
  R7 = Resistor [tolerance=±5% resistance=12k package=THT]
  C1 = Capacitor [part_number=100n package=cap-pth-small]
  R8 = Resistor [tolerance=±5% resistance=10k package=THT]
  JP5 = Header 6 [package=molex-1x6-ra_lock]
  Power_plug1 = Power plug
  JP6 = Header 12 [package=1x12_machine-pin-header_lock.004]
  Q5 = NPN-Transistor [part_number=2N3904 package="TO92 [THT]"]
  Q6 = NPN-Transistor [part_number=2N3904 package="TO92 [THT]"]
  Q4 = NPN-Transistor [part_number=2N3904 package="TO92 [THT]"]
  Q7 = NPN-Transistor [part_number=2N3904 package="TO92 [THT]"]
  Q8 = NPN-Transistor [part_number=2N3904 package="TO92 [THT]"]
  Q9 = NPN-Transistor [part_number=2N3904 package="TO92 [THT]"]
  U1 = ESP8266 WiFi Module [part_number=ESP8266]

nets:
  N1: R2.Pin_0, JP6.8
  N2: R2.Pin_1, Q9.B
  N3: R3.Pin_0, JP6.5
  N4: R3.Pin_1, Q8.B
  N5: R4.Pin_0, Q7.B
  N6: R4.Pin_1, JP6.7
  N7: R5.Pin_0, Q4.B
  N8: R5.Pin_1, JP6.6
  N9: R6.Pin_0, Q5.B
  N10: R6.Pin_1, JP5.5, Q6.E
  N11: R7.Pin_0, JP5.1, Q5.E
  N12: R7.Pin_1, Q6.B
  N13: C1.1, Q6.C, U1.RST
  GND: C1.2, JP5.6, Power_plug1.GND, JP6.10, Q4.E, Q7.E, Q8.E, Q9.E, U1.GND
  N14: R8.Pin_0, Q8.C, U1.IO16
  VCC: R8.Pin_1, Power_plug1.VCC, JP6.9, U1.3.3V
  N15: JP5.2, U1.TX
  N16: JP5.3, U1.RX
  N17: JP6.1, U1.IO14
  N18: JP6.2, U1.IO12
  N19: JP6.3, U1.IO5
  N20: JP6.4, U1.IO4
  N21: Q5.C, Q4.C, U1.IO0
  N22: Q7.C, U1.IO2
  N23: Q9.C, U1.IO13

custom parts:
  ESP8266 WiFi Module: Generic WiFi Module based on the ESP8266
